# Fritzing sketch dragon_scales (saved by Fritzing 1.0.4)
circuit board: 10.5807cm x 9.67299cm
breadboards: 1

parts:
  Col1 = female pin header, 1 pin [form="♀ (female)"]
  Col2 = female pin header, 1 pin [form="♀ (female)"]
  Col3 = female pin header, 1 pin [form="♀ (female)"]
  Col4 = female pin header, 1 pin [form="♀ (female)"]
  Col5 = female pin header, 1 pin [form="♀ (female)"]
  Row1 = female pin header, 1 pin [form="♀ (female)"]
  Row2 = female pin header, 1 pin [form="♀ (female)"]
  Row3 = female pin header, 1 pin [form="♀ (female)"]
  Row4 = female pin header, 1 pin [form="♀ (female)"]
  Row5 = female pin header, 1 pin [form="♀ (female)"]
  D1 = Rectifier Diode [part_number=1N4148 package="300 mil [THT]"]
  D2 = Rectifier Diode [part_number=1N4148 package="300 mil [THT]"]
  D3 = Rectifier Diode [part_number=1N4148 package="300 mil [THT]"]
  D4 = Rectifier Diode [part_number=1N4148 package="300 mil [THT]"]
  D5 = Rectifier Diode [part_number=1N4148 package="300 mil [THT]"]
  D6 = Rectifier Diode [part_number=1N4148 package="300 mil [THT]"]
  D7 = Rectifier Diode [part_number=1N4148 package="300 mil [THT]"]
  D8 = Rectifier Diode [part_number=1N4148 package="300 mil [THT]"]
  D9 = Rectifier Diode [part_number=1N4148 package="300 mil [THT]"]
  D10 = Rectifier Diode [part_number=1N4148 package="300 mil [THT]"]
  D11 = Rectifier Diode [part_number=1N4148 package="300 mil [THT]"]
  D12 = Rectifier Diode [part_number=1N4148 package="300 mil [THT]"]
  D13 = Rectifier Diode [part_number=1N4148 package="300 mil [THT]"]
  D14 = Rectifier Diode [part_number=1N4148 package="300 mil [THT]"]
  D15 = Rectifier Diode [part_number=1N4148 package="300 mil [THT]"]
  D16 = Rectifier Diode [part_number=1N4148 package="300 mil [THT]"]
  D17 = Rectifier Diode [part_number=1N4148 package="300 mil [THT]"]
  D18 = Rectifier Diode [part_number=1N4148 package="300 mil [THT]"]
  D19 = Rectifier Diode [part_number=1N4148 package="300 mil [THT]"]
  D20 = Rectifier Diode [part_number=1N4148 package="300 mil [THT]"]
  D21 = Rectifier Diode [part_number=1N4148 package="300 mil [THT]"]
  D22 = Rectifier Diode [part_number=1N4148 package="300 mil [THT]"]
  D23 = Rectifier Diode [part_number=1N4148 package="300 mil [THT]"]
  D24 = Rectifier Diode [part_number=1N4148 package="300 mil [THT]"]
  D25 = Rectifier Diode [part_number=1N4148 package="300 mil [THT]"]
  S1_1 = Round Pushbutton
  S1_2 = Round Pushbutton
  S1_3 = Round Pushbutton
  S1_4 = Round Pushbutton
  S1_5 = Round Pushbutton
  S2_1 = Round Pushbutton
  S2_2 = Round Pushbutton
  S2_3 = Round Pushbutton
  S2_4 = Round Pushbutton
  S2_5 = Round Pushbutton
  S3_1 = Round Pushbutton
  S3_2 = Round Pushbutton
  S3_3 = Round Pushbutton
  S3_4 = Round Pushbutton
  S3_5 = Round Pushbutton
  S4_1 = Round Pushbutton
  S4_2 = Round Pushbutton
  S4_3 = Round Pushbutton
  S4_4 = Round Pushbutton
  S4_5 = Round Pushbutton
  S5_1 = Round Pushbutton
  S5_2 = Round Pushbutton
  S5_3 = Round Pushbutton
  S5_4 = Round Pushbutton
  S5_5 = Round Pushbutton

nets:
  N1: Col1.pin1, D1.anode, D2.anode, D3.anode, D4.anode, D5.anode
  N2: Col2.pin1, D6.anode, D7.anode, D8.anode, D9.anode, D10.anode
  N3: Col3.pin1, D11.anode, D12.anode, D13.anode, D14.anode, D15.anode
  N4: Col4.pin1, D16.anode, D17.anode, D18.anode, D19.anode, D20.anode
  N5: Col5.pin1, D21.anode, D22.anode, D23.anode, D24.anode, D25.anode
  N6: Row1.pin1, S1_1.leg0, S1_2.leg0, S1_3.leg0, S1_4.leg0, S1_5.leg0
  N7: Row2.pin1, S2_1.leg0
  N8: Row3.pin1, S3_1.leg0, S3_2.leg0, S3_3.leg0, S3_4.leg0, S3_5.leg0
  N9: Row4.pin1, S4_1.leg0, S4_2.leg0, S4_3.leg0, S4_4.leg0, S4_5.leg0
  N10: Row5.pin1, S5_1.leg0, S5_2.leg0, S5_3.leg0, S5_4.leg0, S5_5.leg0
  N11: D1.cathode, S1_1.leg1
  N12: D2.cathode, S2_1.leg1
  N13: D3.cathode, S3_1.leg1
  N14: D4.cathode, S4_1.leg1
  N15: D5.cathode, S5_1.leg1
  N16: D6.cathode, S1_2.leg1
  N17: D7.cathode, S2_2.leg1
  N18: D8.cathode, S3_2.leg1
  N19: D9.cathode, S4_2.leg1
  N20: D10.cathode, S5_2.leg1
  N21: D11.cathode, S1_3.leg1
  N22: D12.cathode, S2_3.leg1
  N23: D13.cathode, S3_3.leg1
  N24: D14.cathode, S4_3.leg1
  N25: D15.cathode, S5_3.leg1
  N26: D16.cathode, S1_4.leg1
  N27: D17.cathode, S2_4.leg1
  N28: D18.cathode, S3_4.leg1
  N29: D19.cathode, S4_4.leg1
  N30: D20.cathode, S5_4.leg1
  N31: D21.cathode, S1_5.leg1
  N32: D22.cathode, S2_5.leg1
  N33: D23.cathode, S3_5.leg1
  N34: D24.cathode, S4_5.leg1
  N35: D25.cathode, S5_5.leg1
  N36: S2_2.leg0, S2_3.leg0, S2_4.leg0, S2_5.leg0
