# Fritzing sketch hackbots_operator (saved by Fritzing 1.0.4)
circuit board: 8.05782cm x 9.37333cm
breadboards: 1

parts:
  1_1 = Pushbutton [package="[THT]"]
  1_2 = Pushbutton [package="[THT]"]
  1_3 = Pushbutton [package="[THT]"]
  1_4 = Pushbutton [package="[THT]"]
  1_5 = Pushbutton [package="[THT]"]
  2_1 = Pushbutton [package="[THT]"]
  2_2 = Pushbutton [package="[THT]"]
  2_3 = Pushbutton [package="[THT]"]
  2_4 = Pushbutton [package="[THT]"]
  2_5 = Pushbutton [package="[THT]"]
  3_1 = Pushbutton [package="[THT]"]
  3_2 = Pushbutton [package="[THT]"]
  3_3 = Pushbutton [package="[THT]"]
  3_4 = Pushbutton [package="[THT]"]
  3_5 = Pushbutton [package="[THT]"]
  4_1 = Pushbutton [package="[THT]"]
  4_2 = Pushbutton [package="[THT]"]
  4_3 = Pushbutton [package="[THT]"]
  4_4 = Pushbutton [package="[THT]"]
  4_5 = Pushbutton [package="[THT]"]
  5_1 = Pushbutton [package="[THT]"]
  5_2 = Pushbutton [package="[THT]"]
  5_3 = Pushbutton [package="[THT]"]
  5_4 = Pushbutton [package="[THT]"]
  5_5 = Pushbutton [package="[THT]"]
  Col1 = female pin header, 1 pin [form="♀ (female)"]
  Col2 = female pin header, 1 pin [form="♀ (female)"]
  Col3 = female pin header, 1 pin [form="♀ (female)"]
  Col4 = female pin header, 1 pin [form="♀ (female)"]
  Col5 = female pin header, 1 pin [form="♀ (female)"]
  Row1 = female pin header, 1 pin [form="♀ (female)"]
  Row2 = female pin header, 1 pin [form="♀ (female)"]
  Row3 = female pin header, 1 pin [form="♀ (female)"]
  Row4 = female pin header, 1 pin [form="♀ (female)"]
  Row5 = female pin header, 1 pin [form="♀ (female)"]
  D1 = Rectifier Diode [part_number=1N4148 package="300 mil [THT]"]
  D2 = Rectifier Diode [part_number=1N4148 package="300 mil [THT]"]
  D3 = Rectifier Diode [part_number=1N4148 package="300 mil [THT]"]
  D4 = Rectifier Diode [part_number=1N4148 package="300 mil [THT]"]
  D5 = Rectifier Diode [part_number=1N4148 package="300 mil [THT]"]
  D6 = Rectifier Diode [part_number=1N4148 package="300 mil [THT]"]
  D7 = Rectifier Diode [part_number=1N4148 package="300 mil [THT]"]
  D8 = Rectifier Diode [part_number=1N4148 package="300 mil [THT]"]
  D9 = Rectifier Diode [part_number=1N4148 package="300 mil [THT]"]
  D10 = Rectifier Diode [part_number=1N4148 package="300 mil [THT]"]
  D11 = Rectifier Diode [part_number=1N4148 package="300 mil [THT]"]
  D12 = Rectifier Diode [part_number=1N4148 package="300 mil [THT]"]
  D13 = Rectifier Diode [part_number=1N4148 package="300 mil [THT]"]
  D14 = Rectifier Diode [part_number=1N4148 package="300 mil [THT]"]
  D15 = Rectifier Diode [part_number=1N4148 package="300 mil [THT]"]
  D16 = Rectifier Diode [part_number=1N4148 package="300 mil [THT]"]
  D17 = Rectifier Diode [part_number=1N4148 package="300 mil [THT]"]
  D18 = Rectifier Diode [part_number=1N4148 package="300 mil [THT]"]
  D19 = Rectifier Diode [part_number=1N4148 package="300 mil [THT]"]
  D20 = Rectifier Diode [part_number=1N4148 package="300 mil [THT]"]
  D21 = Rectifier Diode [part_number=1N4148 package="300 mil [THT]"]
  D22 = Rectifier Diode [part_number=1N4148 package="300 mil [THT]"]
  D23 = Rectifier Diode [part_number=1N4148 package="300 mil [THT]"]
  D24 = Rectifier Diode [part_number=1N4148 package="300 mil [THT]"]
  D25 = Rectifier Diode [part_number=1N4148 package="300 mil [THT]"]

nets:
  N1: 1_1.Pin_2, D1.cathode
  N2: 1_1.Pin_3, 1_1.Pin_4, 1_2.Pin_3, 1_2.Pin_4, 1_3.Pin_3, 1_3.Pin_4, 1_4.Pin_3, 1_4.Pin_4, 1_5.Pin_3, 1_5.Pin_4, Row1.pin1
  N3: 1_2.Pin_2, D6.cathode
  N4: 1_3.Pin_2, D11.cathode
  N5: 1_4.Pin_2, D16.cathode
  N6: 1_5.Pin_2, D21.cathode
  N7: 2_1.Pin_2, D2.cathode
  N8: 2_1.Pin_3, 2_1.Pin_4, 2_2.Pin_3, 2_2.Pin_4, 2_3.Pin_3, 2_3.Pin_4, 2_4.Pin_3, 2_4.Pin_4, 2_5.Pin_3, 2_5.Pin_4, Row2.pin1
  N9: 2_2.Pin_2, D7.cathode
  N10: 2_3.Pin_2, D12.cathode
  N11: 2_4.Pin_2, D17.cathode
  N12: 2_5.Pin_2, D22.cathode
  N13: 3_1.Pin_2, D3.cathode
  N14: 3_1.Pin_3, 3_1.Pin_4, 3_2.Pin_3, 3_2.Pin_4, 3_3.Pin_3, 3_3.Pin_4, 3_4.Pin_3, 3_4.Pin_4, 3_5.Pin_3, 3_5.Pin_4, Row3.pin1
  N15: 3_2.Pin_2, D8.cathode
  N16: 3_3.Pin_2, D13.cathode
  N17: 3_4.Pin_2, D18.cathode
  N18: 3_5.Pin_2, D23.cathode
  N19: 4_1.Pin_2, D4.cathode
  N20: 4_1.Pin_3, 4_1.Pin_4, 4_2.Pin_3, 4_2.Pin_4, 4_3.Pin_3, 4_3.Pin_4, 4_4.Pin_3, 4_4.Pin_4, 4_5.Pin_3, 4_5.Pin_4, Row4.pin1
  N21: 4_2.Pin_2, D9.cathode
  N22: 4_3.Pin_2, D14.cathode
  N23: 4_4.Pin_2, D19.cathode
  N24: 4_5.Pin_2, D24.cathode
  N25: 5_1.Pin_2, D5.cathode
  N26: 5_1.Pin_3, 5_1.Pin_4, 5_2.Pin_3, 5_2.Pin_4, 5_3.Pin_3, 5_3.Pin_4, 5_4.Pin_3, 5_4.Pin_4, 5_5.Pin_3, 5_5.Pin_4, Row5.pin1
  N27: 5_2.Pin_2, D10.cathode
  N28: 5_3.Pin_2, D15.cathode
  N29: 5_4.Pin_2, D20.cathode
  N30: 5_5.Pin_2, D25.cathode
  N31: Col1.pin1, D1.anode, D2.anode, D3.anode, D4.anode, D5.anode
  N32: Col2.pin1, D6.anode, D7.anode, D8.anode, D9.anode, D10.anode
  N33: Col3.pin1, D11.anode, D12.anode, D13.anode, D14.anode, D15.anode
  N34: Col4.pin1, D16.anode, D17.anode, D18.anode, D19.anode, D20.anode
  N35: Col5.pin1, D21.anode, D22.anode, D23.anode, D24.anode, D25.anode
